# Fritzing sketch AkıllıEvProje (saved by Fritzing 0.9.3b)
breadboards: 1

parts:
  Parça1 = Arduino Uno (Rev3)
  BT1 = Bluetooth HC-06u [package=THT]
  LED1 = LEDs [package=led10mm]
  L1 = Solenoid
  LED2 = LEDs [package=led10mm]
  LED3 = LEDs [package=led10mm]
  U1 = 4-Channel 5v Relay Shield [package=relay-4ch5v10a]
  Parça2 = Lilypad Battery Connect

nets:
  N1: Parça1.D8, U1.IN1
  N2: Parça1.D9_PWM, U1.IN2
  N3: Parça1.D10_PWM/SS, Parça1.D11_PWM/MOSI, U1.IN4
  N4: Parça1.D0/RX, BT1.TXD
  N5: Parça1.D1/TX, BT1.RXD
  VCC: Parça1.5V, BT1.VCC, U1.VCC
  GND: Parça1.GND, BT1.GND, U1.GND
  N6: LED1.C, U1.K1-On
  N7: L1.pin2, U1.K2-On
  N8: LED2.C, U1.K3-On
  N9: LED3.A, Parça2.-
  N10: LED3.C, U1.K4-On
  N11: U1.K1-Off, Parça2.+

custom parts:
  Bluetooth HC-06u: Bluetooth HC-06 - face up, pins down 16.5mm x 37.5mm PCB
  LEDs: LEDs Standard schematic elements and footprints for 5mm, 3mm, 1206, and 0603 sized LEDs. 5mm - Spark Fun Electronics SKU : COM-00529 (and others)
  4-Channel 5v Relay Shield: 4 Channel 5v Relay Shield w. 2x SPD-06VDC-SD-C
