# Fritzing sketch BluetoothAracCizim (saved by Fritzing 0.9.3b)

parts:
  Parça1 = Arduino Uno (Rev3)  # not connected
  Parça2 = Rotoshield - Motor driver shield for Arduino
  M1 = DC Motor
  M2 = DC Motor
  M3 = DC Motor
  M4 = DC Motor
  BT1 = Bluetooth HC-06u [package=THT]

nets:
  N1: Parça2.DIG_0, BT1.TXD
  N2: Parça2.DIG_1, BT1.RXD
  +5V: Parça2.+5V, BT1.VCC
  GND: Parça2.GND, BT1.GND
  N3: Parça2.M1-2, M3.pin_2
  N4: Parça2.M1-1, M3.pin_1
  N5: Parça2.M2-2, M4.pin_1
  N6: Parça2.M2-1, M4.pin_2
  N7: Parça2.M3-2, M1.pin_2
  N8: Parça2.M3-1, M1.pin_1
  N9: Parça2.M4-2, M2.pin_2
  N10: Parça2.M4-1, M2.pin_1

custom parts:
  Bluetooth HC-06u: Bluetooth HC-06 - face up, pins down 16.5mm x 37.5mm PCB
