# Fritzing sketch GunesSokakPanelÇizimi (saved by Fritzing 0.9.3b)

parts:
  Parça6 = Lilypad Battery Connect  # not connected
  Parça8 = Lilypad Battery Connect  # not connected
  Parça9 = LilyPad Coin Cell Battery Holder
  Mod3 = Solar Charge Controller [part_number="KLD Series Solar Charge Controller PWM" package=PWM-Model]
  Part4 = Solar Panel [package="Renogy 50 Watts 12 Volt Monocrystalline Bendable Solar Panel"]
  BAT2 = 12 battery [package=battery]
  Mod4 = Solar Charge Controller [part_number="KLD Series Solar Charge Controller PWM" package=PWM-Model]
  X4 = USB Connectors [package=usb-minib-nostop]  # not connected
  Parça10 = Arduino Uno (Rev3)
  LED1 = LEDs [package=led10mm]
  R1 = Photocell (LDR) [package=THT]
  KY-1 = Keyes Relay [package=THT]
  R2 = Resistor [tolerance=±5% resistance=220 package=THT]
  Part5 = Solar Panel [package="Renogy 50 Watts 12 Volt Monocrystalline Bendable Solar Panel"]  # not connected

nets:
  N1: Parça9.+, LED1.A, KY-1.C
  N2: Mod3.Connector_5, BAT2.-, Mod4.Connector_4
  N3: Mod3.Connector_6, BAT2.+, Mod4.Connector_3
  N4: Part4.Connector_1, Mod4.Connector_1
  N5: Part4.Connector_2, Mod4.Connector_2
  N6: Parça10.A0, R2.Pin_0
  N7: Parça10.D8, KY-1.signal
  N8: Parça10.5V, R1.pin_0
  N9: Parça10.GND, R2.Pin_1
  N10: LED1.C, KY-1.NO

custom parts:
  Solar Charge Controller: PWM-Solar Charge Controller
  Solar Panel: Renogy 50 Watts 12 Volt Solar Panel
  12 battery: 12V lead acid type battery, like the Husqvarna YTH2448 12V 35AH battery. The pads in pcb are sized to accomidate up to 14ga wire (as these batterys will deliver high currents.)
  LEDs: LEDs Standard schematic elements and footprints for 5mm, 3mm, 1206, and 0603 sized LEDs. 5mm - Spark Fun Electronics SKU : COM-00529 (and others)
  Keyes Relay: The Keyes 5V relay module is suitable for SCM development, home appliance control. It uses a 5V~12V TIL control signal which can control DC / AC signal.
