# Fritzing sketch HırsızAlarmÇizim (saved by Fritzing 0.9.3b)
breadboards: 1

parts:
  Parça1 = Arduino Uno (Rev3)
  LED1 = LEDs [package=led10mm]
  KY-1 = Keyes Relay [package=THT]
  Parça2 = Lilypad Battery Connect
  J1 = Piezo Speaker
  Parça3 = HC-SR501 Body Sensor Module
  J2 = Basic Servo
  FC-1 = Sound Sensor

nets:
  N1: Parça1.A0, FC-1.OUT
  N2: Parça1.D8, J1.pin2
  N3: Parça1.D10_PWM/SS, KY-1.signal
  N4: Parça1.D5_PWM, Parça3.OUT
  N5: Parça1.D6_PWM, J2.pulse
  VCC: Parça1.5V, KY-1.power, Parça3.VCC, J2.vcc, FC-1.VCC
  GND: Parça1.GND, KY-1.ground, J1.pin1, Parça3.GND, J2.gnd, FC-1.GND
  N6: LED1.A, Parça2.-
  N7: LED1.C, KY-1.NO
  N8: KY-1.C, Parça2.+

custom parts:
  LEDs: LEDs Standard schematic elements and footprints for 5mm, 3mm, 1206, and 0603 sized LEDs. 5mm - Spark Fun Electronics SKU : COM-00529 (and others)
  Keyes Relay: The Keyes 5V relay module is suitable for SCM development, home appliance control. It uses a 5V~12V TIL control signal which can control DC / AC signal.
  HC-SR501 Body Sensor Module: Pyroelectric Infrared PIR Motion Sensor Detector Module
