# Fritzing sketch SokakLambasıÇizim (saved by Fritzing 0.9.3b)
breadboards: 1

parts:
  Parça1 = Arduino Uno (Rev3)
  LED1 = LEDs [package=led10mm]
  KY-1 = Keyes Relay [package=THT]
  Parça2 = Lilypad Battery Connect
  R1 = Photocell (LDR) [package=THT]
  R2 = Resistor [tolerance=±5% resistance=220 package=THT]

nets:
  N1: Parça1.A0, R1.pin_1, R2.Pin_0
  N2: Parça1.D8, KY-1.signal
  N3: Parça1.5V, KY-1.power, R1.pin_0
  N4: Parça1.GND, KY-1.ground, R2.Pin_1
  N5: LED1.A, Parça2.-
  N6: LED1.C, KY-1.NO
  N7: KY-1.C, Parça2.+

custom parts:
  LEDs: LEDs Standard schematic elements and footprints for 5mm, 3mm, 1206, and 0603 sized LEDs. 5mm - Spark Fun Electronics SKU : COM-00529 (and others)
  Keyes Relay: The Keyes 5V relay module is suitable for SCM development, home appliance control. It uses a 5V~12V TIL control signal which can control DC / AC signal.
