# Fritzing sketch YagmurAlarmProje (saved by Fritzing 0.9.3b)
breadboards: 1

parts:
  Parça1 = Arduino Uno (Rev3)
  Water_Level_Sensor1 = Water Level Sensor
  J1 = Basic Servo
  J2 = Piezo Speaker
  LED1 = LEDs [package=led10mm]
  R1 = Resistor [tolerance=±5% resistance=220 package=THT]
  LED2 = LED - 5mm [color="Red (633nm)" package="5 mm [THT]"]

nets:
  N1: Parça1.A0, Water_Level_Sensor1.SIG
  N2: Parça1.D8, J2.pin2
  N3: Parça1.D9_PWM, J1.pulse
  N4: Parça1.D10_PWM/SS, R1.Pin_1
  N5: Parça1.D11_PWM/MOSI, LED1.A
  VCC: Parça1.5V, Water_Level_Sensor1.VCC, J1.vcc
  GND: Parça1.GND, Water_Level_Sensor1.GND, J1.gnd, J2.pin1, LED1.C, LED2.cathode

custom parts:
  Water Level Sensor: A water level sensor. This sensor operates at 3V to 5V. The Sig (signal) pin outputs an analogue signal that is in proportion to the amount of water in contact with the sensor.
